// Logisim project TallerLogica_Combinatorios.circ as structural Verilog: 14 circuits, main circuit sumador_simple
module sumador_simple (
  input  A,
  input  B,
  output S,
  output Cout
);

  xor xor_1 (S, A, B);
  and and_1 (Cout, A, B);
endmodule

module sumador_completo (
  input  Cin,
  input  A,
  input  B,
  output S,
  output Cout
);

  wire sumador_simple_1_cout, sumador_simple_1_s, sumador_simple_2_cout;

  sumador_simple sumador_simple_1 (.A(A), .B(B), .S(sumador_simple_1_s), .Cout(sumador_simple_1_cout));
  sumador_simple sumador_simple_2 (.A(Cin), .B(sumador_simple_1_s), .S(S), .Cout(sumador_simple_2_cout));
  or or_1 (Cout, sumador_simple_2_cout, sumador_simple_1_cout);
endmodule

module sumador_4 (
  input  Cin,
  input  [3:0] A,
  input  [3:0] B,
  output [3:0] S,
  output Cout
);

  wire sumador_completo_1_cout, sumador_completo_2_cout, sumador_completo_3_cout;

  sumador_completo sumador_completo_1 (.Cin(Cin), .A(A[0]), .B(B[0]), .S(S[0]), .Cout(sumador_completo_1_cout));
  sumador_completo sumador_completo_2 (
    .Cin(sumador_completo_1_cout), .A(A[1]), .B(B[1]), .S(S[1]), .Cout(sumador_completo_2_cout));
  sumador_completo sumador_completo_3 (
    .Cin(sumador_completo_2_cout), .A(A[2]), .B(B[2]), .S(S[2]), .Cout(sumador_completo_3_cout));
  sumador_completo sumador_completo_4 (.Cin(sumador_completo_3_cout), .A(A[3]), .B(B[3]), .S(S[3]), .Cout(Cout));
  Hex_Digit_Display hex_digit_display_1 (.value(S));  // open: dp
endmodule

module comparador_cero (
  input  [3:0] A,
  output Z
);

  wire and_1_out, and_2_out, not_1_out, not_2_out, not_3_out, not_4_out;

  not not_1 (not_1_out, A[0]);
  not not_2 (not_2_out, A[1]);
  not not_3 (not_3_out, A[2]);
  not not_4 (not_4_out, A[3]);
  and and_1 (and_1_out, not_1_out, not_2_out);
  and and_2 (and_2_out, not_3_out, not_4_out);
  and and_3 (Z, and_1_out, and_2_out);
endmodule

module sumador_flags (
  input  Cin,
  input  [3:0] A,
  input  [3:0] B,
  output [3:0] S,
  output Z,
  output C,
  output V,
  output N
);

  sumador_4 sumador_4_1 (.Cin(Cin), .A(A), .B(B), .S(S), .Cout(C));
  Hex_Digit_Display hex_digit_display_1 (.value(S));  // open: dp
  comparador_cero comparador_cero_1 (.A(S), .Z(Z));
  overflow_check overflow_check_1 (.A(A), .B(B), .Sum(S), .S(V));
  is_negative is_negative_1 (.A(S), .N(N));
endmodule

module incrementador_4 (
  input  [3:0] A,
  output [3:0] S
);

  wire not_1_out, not_2_out, or_1_out;

  not not_1 (not_1_out, A[3]);
  not not_2 (not_2_out, not_1_out);
  or or_1 (or_1_out, not_1_out, not_2_out);
  Hex_Digit_Display hex_digit_display_1 (.value(S));  // open: dp
  sumador_4 sumador_4_1 (.Cin(or_1_out), .B(A), .S(S));  // open: A, Cout
endmodule

module inversor_4 (
  input  [3:0] A,
  input  INV,
  output [3:0] S
);

  wire [3:0] incrementador_4_1_s, not_byte_1_s;

  not_byte not_byte_1 (.A(A), .S(not_byte_1_s));
  incrementador_4 incrementador_4_1 (.A(not_byte_1_s), .S(incrementador_4_1_s));
  Multiplexer #(.width(4)) multiplexer_1 (.in0(A), .in1(incrementador_4_1_s), .out(S), .sel(INV));
  Hex_Digit_Display hex_digit_display_1 (.value(S));  // open: dp
endmodule

module ALU (
  input  [3:0] A,
  input  [3:0] B,
  input  [1:0] OP,
  output N,
  output Z,
  output V,
  output C,
  output [3:0] S
);

  wire sumador_flags_1_c, sumador_flags_1_v, sumador_flags_1_z, sumador_flags_2_c, sumador_flags_2_v;
  wire [3:0] and_byte_1_s, inversor_4_1_s, or_byte_1_s, sumador_flags_1_s, sumador_flags_2_s;

  sumador_flags sumador_flags_1 (
    .A(A), .B(B), .S(sumador_flags_1_s), .Z(sumador_flags_1_z), .C(sumador_flags_1_c), .V(sumador_flags_1_v));  // open: Cin, N
  inversor_4 inversor_4_1 (.A(B), .INV(1'b1), .S(inversor_4_1_s));
  and_byte and_byte_1 (.A(A), .B(B), .S(and_byte_1_s));
  or_byte or_byte_1 (.A(A), .B(B), .S(or_byte_1_s));
  sumador_flags sumador_flags_2 (
    .A(A), .B(inversor_4_1_s), .S(sumador_flags_2_s), .C(sumador_flags_2_c), .V(sumador_flags_2_v));  // open: Cin, Z, N
  Multiplexer #(.select(2), .width(4)) multiplexer_1 (
    .in0(sumador_flags_1_s), .in1(sumador_flags_2_s), .in2(and_byte_1_s), .in3(or_byte_1_s), .out(S), .sel(OP));
  Multiplexer #(.select(2)) multiplexer_2 (
    .in0(sumador_flags_1_c), .in1(sumador_flags_2_c), .in2(1'b0), .in3(1'b0), .out(C), .sel(OP));
  Multiplexer #(.select(2)) multiplexer_3 (
    .in0(sumador_flags_1_v), .in1(sumador_flags_2_v), .in2(1'b0), .in3(1'b0), .out(V), .sel(OP));
  Hex_Digit_Display hex_digit_display_1 (.value(S));  // open: dp
  is_negative is_negative_1 (.A(S), .N(N));
  comparador_cero comparador_cero_1 (.A(S), .Z(Z));
endmodule

module verificador (
  output [3:0] out_1,
  output [3:0] out_2,
  output [1:0] out_3,
  output halt,
  output N,
  output Z,
  output V,
  output C,
  output [3:0] res
);

  wire clock_1_out;

  Clock clock_1 (.out(clock_1_out));
  Counter #(.max('h3ff), .width(10)) counter_1 (
    .clk(clock_1_out), .carry(halt), .Q({out_3, out_2, out_1}));  // open: clr, load, up, count, D
  ALU alu_1 (.A(out_1), .B(out_2), .OP(out_3), .N(N), .Z(Z), .V(V), .C(C), .S(res));
endmodule

module not_byte (
  input  [3:0] A,
  output [3:0] S
);

  not not_1 (S[2], A[2]);
  not not_2 (S[3], A[3]);
  not not_3 (S[0], A[0]);
  not not_4 (S[1], A[1]);
  Hex_Digit_Display hex_digit_display_1 (.value(S));  // open: dp
endmodule

module overflow_check (
  input  [3:0] A,
  input  [3:0] B,
  input  [3:0] Sum,
  output S
);

  wire not_1_out, xor_1_out, xor_2_out;

  xor xor_1 (xor_1_out, A[3], B[3]);
  not not_1 (not_1_out, xor_1_out);
  xor xor_2 (xor_2_out, B[3], Sum[3]);
  and and_1 (S, not_1_out, xor_2_out);
endmodule

module and_byte (
  input  [3:0] A,
  input  [3:0] B,
  output [3:0] S
);

  and and_1 (S[0], A[0], B[0]);
  and and_2 (S[1], A[1], B[1]);
  and and_3 (S[2], A[2], B[2]);
  and and_4 (S[3], A[3], B[3]);
endmodule

module or_byte (
  input  [3:0] A,
  input  [3:0] B,
  output [3:0] S
);

  or or_1 (S[0], A[0], B[0]);
  or or_2 (S[1], A[1], B[1]);
  or or_3 (S[2], A[2], B[2]);
  or or_4 (S[3], A[3], B[3]);
endmodule

module is_negative (
  input  [3:0] A,
  output N
);


  assign N = A[3];
endmodule
