// Logisim project sc_modelo.circ as structural Verilog: 15 circuits, main circuit verificador
module sumador_simple (
  input  A,
  input  B,
  output S,
  output Cout
);

  xor xor_1 (S, A, B);
  and and_1 (Cout, A, B);
endmodule

module sumador_completo (
  input  Cin,
  input  A,
  input  B,
  output S,
  output Cout
);

  wire sumador_simple_1_cout, sumador_simple_2_cout, sumador_simple_2_s;

  sumador_simple sumador_simple_1 (.A(sumador_simple_2_s), .B(Cin), .S(S), .Cout(sumador_simple_1_cout));
  sumador_simple sumador_simple_2 (.A(A), .B(B), .S(sumador_simple_2_s), .Cout(sumador_simple_2_cout));
  or or_1 (Cout, sumador_simple_1_cout, sumador_simple_2_cout);
endmodule

module sumador_4 (
  input  Cin,
  input  [3:0] A,
  input  [3:0] B,
  output [3:0] S,
  output Cout
);

  wire sumador_completo_1_cout, sumador_completo_2_cout, sumador_completo_3_cout;

  sumador_completo sumador_completo_1 (.Cin(Cin), .A(A[0]), .B(B[0]), .S(S[0]), .Cout(sumador_completo_1_cout));
  sumador_completo sumador_completo_2 (
    .Cin(sumador_completo_1_cout), .A(A[1]), .B(B[1]), .S(S[1]), .Cout(sumador_completo_2_cout));
  sumador_completo sumador_completo_3 (
    .Cin(sumador_completo_2_cout), .A(A[2]), .B(B[2]), .S(S[2]), .Cout(sumador_completo_3_cout));
  sumador_completo sumador_completo_4 (.Cin(sumador_completo_3_cout), .A(A[3]), .B(B[3]), .S(S[3]), .Cout(Cout));
  Hex_Digit_Display hex_digit_display_1 (.value(S));  // open: dp
endmodule

module comparador_cero (
  input  [3:0] A,
  output Z
);

  wire or_1_out, or_2_out, or_3_out;

  or or_1 (or_1_out, A[0], A[1]);
  or or_2 (or_2_out, A[2], A[3]);
  or or_3 (or_3_out, or_1_out, or_2_out);
  not not_1 (Z, or_3_out);
endmodule

module sumador_flags (
  input  Cin,
  input  [3:0] A,
  input  [3:0] B,
  output [3:0] S,
  output N,
  output Z,
  output V,
  output C
);

  sumador_4 sumador_4_1 (.Cin(Cin), .A(A), .B(B), .S({N, S[2:0]}), .Cout(C));
  Hex_Digit_Display hex_digit_display_1 (.value({N, S[2:0]}));  // open: dp
  comparador_cero comparador_cero_1 (.A({N, S[2:0]}), .Z(Z));
  comp_overflow comp_overflow_1 (.c3(N), .a3(A[3]), .b3(B[3]), .O(V));

  assign S[3] = N;
endmodule

module incrementador_4 (
  input  [3:0] A,
  output [3:0] S
);

  sumador_4 sumador_4_1 (.A(A), .B(4'b0001), .S(S));  // open: Cin, Cout
  Hex_Digit_Display hex_digit_display_1 (.value(S));  // open: dp
endmodule

module inversor_4 (
  input  [3:0] A,
  input  INV,
  output [3:0] S
);

  wire [3:0] incrementador_4_1_s, not_1_out;

  not not_1 (not_1_out[0], A[0]);
  not not_2 (not_1_out[1], A[1]);
  not not_3 (not_1_out[2], A[2]);
  not not_4 (not_1_out[3], A[3]);
  Multiplexer #(.width(4)) multiplexer_1 (.in0(A), .in1(incrementador_4_1_s), .out(S), .sel(INV));
  incrementador_4 incrementador_4_1 (.A(not_1_out), .S(incrementador_4_1_s));
  Hex_Digit_Display hex_digit_display_1 (.value(S));  // open: dp
endmodule

module ALU (
  input  [3:0] A,
  input  [3:0] B,
  input  [1:0] OP,
  output N,
  output Z,
  output V,
  output C,
  output [3:0] S
);

  wire [3:0] AND_FLAGS, OR_FLAGS, RES_FLAGS, S_ADD, S_AND, S_OR, S_RES, SUM_FLAGS;

  sumador_flags sumador_flags_1 (
    .A(A), .B(B), .S(S_ADD), .N(SUM_FLAGS[0]), .Z(SUM_FLAGS[1]), .V(SUM_FLAGS[2]), .C(SUM_FLAGS[3]));  // open: Cin
  restador_flags restador_flags_1 (
    .A(A), .B(B), .S(S_RES), .N(RES_FLAGS[0]), .Z(RES_FLAGS[1]), .V(RES_FLAGS[2]), .C(RES_FLAGS[3]));
  and_4_flags and_4_flags_1 (
    .A(A), .B(B), .S(S_AND), .N(AND_FLAGS[0]), .Z(AND_FLAGS[1]), .V(AND_FLAGS[2]), .C(AND_FLAGS[3]));
  or_4_flags or_4_flags_1 (.A(A), .B(B), .S(S_OR), .N(OR_FLAGS[0]), .Z(OR_FLAGS[1]), .V(OR_FLAGS[2]), .C(OR_FLAGS[3]));
  Multiplexer #(.select(2), .width(4)) multiplexer_1 (
    .in0(SUM_FLAGS), .in1(RES_FLAGS), .in2(AND_FLAGS), .in3(OR_FLAGS), .out({C, V, Z, N}), .sel(OP));
  Multiplexer #(.select(2), .width(4)) multiplexer_2 (
    .in0(S_ADD), .in1(S_RES), .in2(S_AND), .in3(S_OR), .out(S), .sel(OP));
  Hex_Digit_Display hex_digit_display_1 (.value(S));  // open: dp
endmodule

module verificador (
  output [3:0] out_1,
  output [3:0] out_2,
  output [1:0] out_3,
  output halt,
  output N,
  output Z,
  output V,
  output C,
  output [3:0] res
);

  wire clock_1_out;

  Clock clock_1 (.out(clock_1_out));
  Counter #(.max('h3ff), .width(10)) counter_1 (
    .clk(clock_1_out), .carry(halt), .Q({out_3, out_2, out_1}));  // open: clr, load, up, count, D
  ALU alu_1 (.A(out_1), .B(out_2), .OP(out_3), .N(N), .Z(Z), .V(V), .C(C), .S(res));
endmodule

module overflow_resta (
  input  V_in,
  input  [3:0] B,
  output V_out
);

  wire comparador_cero_1_z, not_2_out;
  wire [3:3] not_1_out;

  not not_1 (not_1_out[3], B[3]);
  not not_2 (not_2_out, V_in);
  comparador_cero comparador_cero_1 (.A({not_1_out[3], B[2:0]}), .Z(comparador_cero_1_z));
  Multiplexer multiplexer_1 (.in0(V_in), .in1(not_2_out), .out(V_out), .sel(comparador_cero_1_z));
endmodule

module comp_overflow (
  input  c3,
  input  a3,
  input  b3,
  output O
);

  wire not_1_out, xor_1_out, xor_2_out;

  xor xor_1 (xor_1_out, c3, a3);
  not not_1 (not_1_out, xor_2_out);
  xor xor_2 (xor_2_out, a3, b3);
  and and_1 (O, xor_1_out, not_1_out);
endmodule

module restador_flags (
  input  [3:0] A,
  input  [3:0] B,
  output [3:0] S,
  output N,
  output Z,
  output V,
  output C
);

  wire sumador_flags_1_c, sumador_flags_1_v;
  wire [3:0] inversor_4_1_s;

  inversor_4 inversor_4_1 (.A(B), .INV(1'b1), .S(inversor_4_1_s));
  sumador_flags sumador_flags_1 (
    .A(A), .B(inversor_4_1_s), .S(S), .N(N), .Z(Z), .V(sumador_flags_1_v), .C(sumador_flags_1_c));  // open: Cin
  overflow_resta overflow_resta_1 (.V_in(sumador_flags_1_v), .B(B), .V_out(V));
  Hex_Digit_Display hex_digit_display_1 (.value(S));  // open: dp
  carry_resta carry_resta_1 (.C_in(sumador_flags_1_c), .B(B), .C_out(C));
endmodule

module and_4_flags (
  input  [3:0] A,
  input  [3:0] B,
  output [3:0] S,
  output N,
  output Z,
  output V,
  output C
);

  assign {N, S[2:0]} = A & B;  // AND_Gate and_1, 4 bits wide
  comparador_cero comparador_cero_1 (.A({N, S[2:0]}), .Z(Z));

  assign C = 1'b0;
  assign S[3] = N;
  assign V = 1'b0;
endmodule

module or_4_flags (
  input  [3:0] A,
  input  [3:0] B,
  output [3:0] S,
  output N,
  output Z,
  output V,
  output C
);

  assign {N, S[2:0]} = A | B;  // OR_Gate or_1, 4 bits wide
  comparador_cero comparador_cero_1 (.A({N, S[2:0]}), .Z(Z));

  assign C = 1'b0;
  assign S[3] = N;
  assign V = 1'b0;
endmodule

module carry_resta (
  input  C_in,
  input  [3:0] B,
  output C_out
);

  wire comparador_cero_1_z, not_1_out;

  not not_1 (not_1_out, C_in);
  comparador_cero comparador_cero_1 (.A(B), .Z(comparador_cero_1_z));
  Multiplexer multiplexer_1 (.in0(not_1_out), .in1(C_in), .out(C_out), .sel(comparador_cero_1_z));
endmodule
